# Fritzing sketch Sketch (saved by Fritzing 0.9.2b)
breadboards: 1

parts:
  Raspberry_Pi1 = Raspberry Pi 2
  IC1 = MCP3008 8-channel 10-bit ADC [part_number=MCP3008]
  U1 = TMP36 [package=to-92-kit]
  U2 = 2-Channel 5v Relay Shield [package=relay-2ch5v10a]
  S1 = Round Pushbutton
  S2 = Round Pushbutton

nets:
  N1: Raspberry_Pi1.GPIO10, IC1.no_name_yet#11
  N2: Raspberry_Pi1.GPIO9, IC1.no_name_yet#12
  N3: Raspberry_Pi1.GPIO11, IC1.no_name_yet#13
  N4: Raspberry_Pi1.GPIO5, S1.leg1
  N5: Raspberry_Pi1.GPIO6, S2.leg1
  N6: Raspberry_Pi1.GPIO13, U2.IN1
  GND: Raspberry_Pi1.GND, IC1.no_name_yet#9, IC1.no_name_yet#14, U1.GND, U2.GND, S1.leg0, S2.leg0
  N7: Raspberry_Pi1.GPIO8, IC1.no_name_yet#10
  VCC: Raspberry_Pi1.5V, IC1.no_name_yet#15, IC1.no_name_yet#16, U1.VCC, U2.VCC, U2.IN2
  N8: IC1.no_name_yet#1, U1.VOUT

notes:
  To Garage Door Control Unit
  Door Closed
  Door Opened

custom parts:
  2-Channel 5v Relay Shield: 2 Channel 5v Relay Shield w. 2x SPD-06VDC-SD-C
